// Logisim project lab 1.circ as structural Verilog: 1 circuit, main circuit main
module main (
  input  Cin,
  input  S1,
  input  S0,
  input  A1,
  input  B1,
  input  A2,
  input  B2,
  input  A3,
  input  B3,
  input  A4,
  input  B4
);

  wire adder_1_cout, adder_1_out, adder_2_cout, adder_2_out, adder_3_cout, adder_3_out, adder_4_cout,
       adder_4_out, and_1_out, and_2_out, and_3_out, and_4_out, and_5_out, and_6_out, and_7_out, and_8_out,
       not_1_out, not_2_out, not_3_out, not_4_out, or_1_out, or_2_out, or_3_out, or_4_out;

  not not_1 (not_1_out, B1);
  not not_2 (not_2_out, B2);
  not not_3 (not_3_out, B3);
  not not_4 (not_4_out, B4);
  and and_1 (and_1_out, B1, S0);
  and and_2 (and_2_out, not_1_out, S1);
  and and_3 (and_3_out, B2, S0);
  and and_4 (and_4_out, not_2_out, S1);
  and and_5 (and_5_out, B3, S0);
  and and_6 (and_6_out, not_3_out, S1);
  and and_7 (and_7_out, B4, S0);
  and and_8 (and_8_out, not_4_out, S1);
  or or_1 (or_1_out, and_1_out, and_2_out);
  or or_2 (or_2_out, and_3_out, and_4_out);
  or or_3 (or_3_out, and_5_out, and_6_out);
  or or_4 (or_4_out, and_7_out, and_8_out);
  Adder #(.width(1)) adder_1 (.a(A1), .b(or_1_out), .out(adder_1_out), .cin(Cin), .cout(adder_1_cout));
  Adder #(.width(1)) adder_2 (.a(A2), .b(or_2_out), .out(adder_2_out), .cin(adder_1_cout), .cout(adder_2_cout));
  Adder #(.width(1)) adder_3 (.a(A3), .b(or_3_out), .out(adder_3_out), .cin(adder_2_cout), .cout(adder_3_cout));
  Adder #(.width(1)) adder_4 (.a(A4), .b(or_4_out), .out(adder_4_out), .cin(adder_3_cout), .cout(adder_4_cout));
  LED led_1 (.in(adder_1_out));
  LED led_2 (.in(adder_2_out));
  LED led_3 (.in(adder_3_out));
  LED led_4 (.in(adder_4_out));
  LED led_5 (.in(adder_4_cout));

  // Notes on the sheet:
  //   F1
  //   F2
  //   F3
  //   F4
  //   Cout
endmodule
