// Logisim project lab 2 work.circ as structural Verilog: 1 circuit, main circuit main
module main (
  input  Cin,
  input  S2,
  input  S1,
  input  S0,
  input  A1,
  input  B1,
  input  A2,
  input  B2,
  output out_9,
  output out_10,
  output out_11
);

  wire adder_1_cout, adder_2_cout, and_1_out, and_2_out, and_3_out, and_4_out, and_5_out, and_6_out,
       and_7_out, and_8_out, and_9_out, and_10_out, and_11_out, and_12_out, not_1_out, not_2_out, not_3_out,
       not_4_out, not_5_out, or_1_out, or_2_out, or_3_out, or_4_out;

  not not_1 (not_1_out, S2);
  not not_2 (not_2_out, S0);
  not not_3 (not_3_out, B1);
  not not_4 (not_4_out, B2);
  not not_5 (not_5_out, S1);
  and and_1 (and_1_out, not_2_out, S1, S2);
  and and_2 (and_2_out, not_2_out, not_5_out, S2);
  and and_3 (and_3_out, and_2_out, B1);
  and and_4 (and_4_out, and_1_out, not_3_out);
  and and_5 (and_5_out, B1, S0);
  and and_6 (and_6_out, not_3_out, S1);
  and and_7 (and_7_out, and_2_out, B2);
  and and_8 (and_8_out, and_1_out, not_4_out);
  and and_9 (and_9_out, B2, S0);
  and and_10 (and_10_out, not_4_out, S1);
  or or_1 (or_1_out, and_3_out, and_4_out, A1);
  or or_2 (or_2_out, and_5_out, and_6_out);
  or or_3 (or_3_out, and_7_out, and_8_out, A2);
  or or_4 (or_4_out, and_9_out, and_10_out);
  and and_11 (and_11_out, not_1_out, Cin);
  Adder #(.width(1)) adder_1 (.a(or_1_out), .b(or_2_out), .out(out_9), .cin(and_11_out), .cout(adder_1_cout));
  and and_12 (and_12_out, not_1_out, adder_1_cout);
  and and_13 (out_11, not_1_out, adder_2_cout);
  Adder #(.width(1)) adder_2 (.a(or_3_out), .b(or_4_out), .out(out_10), .cin(and_12_out), .cout(adder_2_cout));
endmodule
